// Logisim project lcd_de0.circ as structural Verilog: 1 circuit, main circuit main
module main (
  output [7:0] LCD_Data,
  output LCD_RW,
  output LCD_EN,
  output LCD_RS,
  output LCD_BLON,
  output LED_RW,
  output LED_EN,
  output LED_RS,
  output LED_BLON
);

  wire clock_1_out;

  Counter counter_1 (
    .clr(1'b0), .load(1'b0), .up(1'b1), .count(1'b1), .clk(clock_1_out), .D({8{1'b0}}), .Q(LCD_Data));  // open: carry
  Clock clock_1 (.out(clock_1_out));
  Hex_Digit_Display Hex_Digit_Display_1 (.value(LCD_Data[7:4]));  // open: dp
  Hex_Digit_Display Hex_Digit_Display_2 (.value(LCD_Data[3:0]));  // open: dp
  Comparator comparator_1 (.a(LCD_Data), .b(8'h10), .lt(LCD_EN));  // open: gt, eq

  assign LCD_BLON = 1'b1;
  assign LCD_RS = 1'b1;
  assign LCD_RW = 1'b0;
  assign LED_BLON = 1'b1;
  assign LED_EN = LCD_EN;
  assign LED_RS = 1'b1;
  assign LED_RW = 1'b0;
endmodule
