// Logisim project slqisc_flash_de0.circ as structural Verilog: 1 circuit, main circuit main
module main (
);

  wire and_1_out, clock_1_out, comparator_1_gt, comparator_2_eq, counter_1_carry, decoder_1_out0,
       decoder_1_out1, decoder_1_out2, decoder_1_out3, decoder_1_out4, decoder_1_out5, decoder_1_out6,
       decoder_1_out7, decoder_2_out1, decoder_2_out2, decoder_2_out3, decoder_2_out4, decoder_2_out5,
       decoder_2_out6, decoder_2_out7, not_1_out, or_1_out, RESET_out;
  wire [2:0] counter_2_q;
  wire [3:0] register_1_q_2;
  wire [11:0] register_1_q;
  wire [13:0] counter_1_q, multiplexer_3_out;
  wire [15:0] adder_1_out, adder_2_out, adder_3_out, Adr_q, bit_extender_1_out, Min_q, MinLoc_q,
       multiplexer_1_out, multiplexer_2_out, multiplexer_4_out, negator_1_out, PC_q, RAM_1_dout, ROM_1_data,
       Sub_q, SubLoc_q;

  Clock clock_1 (.out(clock_1_out));
  Multiplexer #(.width(16)) multiplexer_1 (
    .in0(Adr_q), .in1(adder_2_out), .out(multiplexer_1_out), .sel(comparator_1_gt));
  Comparator #(.width(16)) comparator_1 (.a(adder_3_out), .b({16{1'b0}}), .gt(comparator_1_gt));  // open: eq, lt
  Counter #(.max('h3fff), .ongoal("stay"), .width(14)) counter_1 (
    .clr(RESET_out), .load(1'b0), .up(1'b1), .count(not_1_out), .clk(clock_1_out), .D({14{1'b1}}),
    .carry(counter_1_carry), .Q(counter_1_q));
  Register #(.width(16)) PC (.D(multiplexer_1_out), .en(decoder_2_out7), .clk(clock_1_out), .Q(PC_q), .clr(RESET_out));
  not not_1 (not_1_out, counter_1_carry);
  assign bit_extender_1_out = {{13{1'b0}}, counter_2_q};  // Bit_Extender bit_extender_1
  Counter #(.max('h7), .width(3)) counter_2 (
    .clr(RESET_out), .load(not_1_out), .up(1'b1), .count(counter_1_carry), .clk(clock_1_out), .D(3'b111),
    .Q(counter_2_q));  // open: carry
  ROM #(.addrWidth(14), .dataWidth(16)) ROM_1 (.addr(counter_1_q), .data(ROM_1_data));
  Adder #(.width(16)) adder_1 (.a(PC_q), .b(bit_extender_1_out), .out(adder_1_out));  // open: cin, cout
  Adder #(.width(16)) adder_2 (.a(PC_q), .b(16'h3), .out(adder_2_out));  // open: cin, cout
  Multiplexer #(.select(3), .width(16)) multiplexer_2 (
    .in0(adder_1_out), .in1(adder_1_out), .in2(adder_1_out), .in3(SubLoc_q), .in4(MinLoc_q), .in5(MinLoc_q),
    .in6(MinLoc_q), .out(multiplexer_2_out), .sel(counter_2_q));  // open: in7
  Multiplexer #(.width(14)) multiplexer_3 (
    .in0(counter_1_q), .in1(multiplexer_2_out[13:0]), .out(multiplexer_3_out), .sel(counter_1_carry));
  Multiplexer #(.width(16)) multiplexer_4 (
    .in0(ROM_1_data), .in1(adder_3_out), .out(multiplexer_4_out), .sel(counter_1_carry));
  or or_1 (or_1_out, ~counter_1_carry, decoder_2_out6);  // OR_Gate
  RAM #(.addrWidth(14), .dataWidth(16), .\type ("nonvolatile")) RAM_1 (
    .addr(multiplexer_3_out), .we(or_1_out), .oe(counter_1_carry), .clk(clock_1_out),
    .din(multiplexer_4_out), .dout(RAM_1_dout));
  LED LED_1 (.in(decoder_1_out0));
  LED LED_2 (.in(decoder_1_out1));
  Button RESET (.out(RESET_out));
  Decoder #(.enable("false"), .select(3)) decoder_1 (
    .out0(decoder_1_out0), .out1(decoder_1_out1), .out2(decoder_1_out2), .out3(decoder_1_out3),
    .out4(decoder_1_out4), .out5(decoder_1_out5), .out6(decoder_1_out6), .out7(decoder_1_out7),
    .sel(counter_2_q));
  LED LED_3 (.in(decoder_1_out2));
  LED LED_4 (.in(decoder_1_out3));
  LED LED_5 (.in(decoder_1_out4));
  LED LED_6 (.in(decoder_1_out5));
  LED LED_7 (.in(decoder_1_out6));
  LED LED_8 (.in(decoder_1_out7));
  Decoder #(.enable("false"), .select(3)) decoder_2 (
    .out1(decoder_2_out1), .out2(decoder_2_out2), .out3(decoder_2_out3), .out4(decoder_2_out4),
    .out5(decoder_2_out5), .out6(decoder_2_out6), .out7(decoder_2_out7), .sel(counter_2_q));  // open: out0
  Register #(.trigger("falling"), .width(16)) SubLoc (
    .D(RAM_1_dout), .en(decoder_2_out1), .clk(clock_1_out), .Q(SubLoc_q), .clr(RESET_out));
  Register #(.trigger("falling"), .width(16)) MinLoc (
    .D(RAM_1_dout), .en(decoder_2_out2), .clk(clock_1_out), .Q(MinLoc_q), .clr(RESET_out));
  Register #(.trigger("falling"), .width(16)) Adr (
    .D(RAM_1_dout), .en(decoder_2_out3), .clk(clock_1_out), .Q(Adr_q), .clr(RESET_out));
  Register #(.trigger("falling"), .width(16)) Sub (
    .D(RAM_1_dout), .en(decoder_2_out4), .clk(clock_1_out), .Q(Sub_q), .clr(RESET_out));
  Register #(.trigger("falling"), .width(16)) Min (
    .D(RAM_1_dout), .en(decoder_2_out5), .clk(clock_1_out), .Q(Min_q), .clr(RESET_out));
  Comparator #(.width(16)) comparator_2 (.a(MinLoc_q), .b({16{1'b1}}), .eq(comparator_2_eq));  // open: gt, lt
  Negator #(.width(16)) negator_1 (.in(Sub_q), .out(negator_1_out));
  Adder #(.width(16)) adder_3 (.a(negator_1_out), .b(Min_q), .out(adder_3_out));  // open: cin, cout
  and and_1 (and_1_out, comparator_2_eq, decoder_2_out7);
  Register #(.trigger("falling"), .width(16)) register_1 (
    .D(Sub_q), .en(and_1_out), .clk(clock_1_out), .Q({register_1_q_2, register_1_q}), .clr(RESET_out));
  Hex_Digit_Display Hex_Digit_Display_1 (.value(register_1_q_2));  // open: dp
  Hex_Digit_Display Hex_Digit_Display_2 (.value(register_1_q[11:8]));  // open: dp
  Hex_Digit_Display Hex_Digit_Display_3 (.value(register_1_q[7:4]));  // open: dp
  Hex_Digit_Display Hex_Digit_Display_4 (.value(register_1_q[3:0]));  // open: dp

  // Notes on the sheet:
  //   contents of ROM_1 (hex, n*v repeats v):
  //   95 95 3 94 8f 6 8f 95 9 8f 8f c 13 13 f 12 12 14 0 0 94 8f 17 8f 12 29 8f 8f 1d 90 12 20 95 8f 23 8f
  //   13 26 8f 8f 17 95 95 2c 13 8f 2f 8f 95 32 8f 8f 35 96 96 38 93 8f 3b 8f 96 3e 8f 8f 41 91 96 44 95
  //   96 7a 95 95 4a 93 8f 4d 8f 95 50 8f 8f 53 91 95 56 94 95 5c 8f 8f 56 94 8f 5f 8f 95 62 8f 8f 65 90
  //   95 68 96 96 6b 95 96 6e 95 95 71 96 95 7d 91 94 77 8f 8f 0 93 ffff 7d 91 93 80 94 94 83 92 8f 86 8f
  //   94 89 8f 8f 8c 8f 8f 0 0 1 ffff 2 2 2
endmodule
